// Logisim project full_adder.circ as structural Verilog: 1 circuit, main circuit main
module main (
  input  in_1,
  input  in_2,
  input  in_3,
  output SUM,
  output Cout
);

  wire and_1_out, and_2_out, xor_1_out;

  xor xor_1 (xor_1_out, in_1, in_2);
  and and_1 (and_1_out, in_1, in_2);
  xor xor_2 (SUM, xor_1_out, in_3);
  and and_2 (and_2_out, xor_1_out, in_3);
  or or_1 (Cout, and_1_out, and_2_out, and_2_out);

  // Notes on the sheet:
  //   Cin
  //   FULL ADDER
endmodule
