// Logisim project half_adder.circ as structural Verilog: 1 circuit, main circuit main
module main (
  input  in_1,
  input  in_2,
  output SUM,
  output Carry
);

  xor xor_1 (SUM, in_1, in_2);
  and and_1 (Carry, in_2, in_1);
endmodule
