// Logisim project half_subtractor.circ as structural Verilog: 1 circuit, main circuit main
module main (
  input  A,
  input  in_2,
  output A_B,
  output A_B_2
);

  wire not_1_out;

  not not_1 (not_1_out, A);
  xor xor_1 (A_B, A, in_2);
  and and_1 (A_B_2, not_1_out, in_2);

  // Notes on the sheet:
  //   B
  //   HALF SUBTRACTOR
endmodule
